# Fritzing sketch pumpkin_shield (saved by Fritzing 0.9.10b)
circuit board: 8.46667cm x 5.64444cm

parts:
  Part1 = Arduino Prototyping Shield
  LED1 = LED - 5mm [color="Red (633nm)" current=0.030 package="5 mm [THT]"]
  LED2 = LED - 5mm [color="Blue (470nm)" current=0.030 package="5 mm [THT]"]
  LED3 = LED - 5mm [color="White (6500K)" current=0.030 package="5 mm [THT]"]
  R1 = Resistor [tolerance=±5% power=0.25 resistance=220 package=THT]
  R2 = Resistor [tolerance=±5% power=0.25 resistance=220 package=THT]
  R3 = Resistor [tolerance=±5% power=0.25 resistance=220 package=THT]

nets:
  N1: Part1.D5, R3.Pin_0
  N2: Part1.GND, Part1.N$143, Part1.N$268, Part1.N$304, LED1.cathode, LED2.cathode, LED3.cathode
  N3: Part1.D6, R2.Pin_0
  N4: Part1.D7, R1.Pin_0
  N5: Part1.N$229, Part1.N$230, LED2.anode, R1.Pin_1
  N6: Part1.N$312, Part1.N$313, LED1.anode, R2.Pin_1
  N7: Part1.N$402, Part1.N$408, LED3.anode, R3.Pin_1
